# Fritzing sketch Wiring (saved by Fritzing 0.9.3b)

parts:
  JP1 = USB_MICROB_PLUG [package=micro-b-ra-th]
  Bauteil1 = Arduino Nano (Rev3.0)
  hc-sr1 = hc-sr04
  hc-sr2 = hc-sr04
  NEOPIXEL1 = Neopixel Strip -- Black (30/m)
  NEOPIXEL2 = Neopixel Strip -- Black (30/m)
  C1 = Electrolytic Capacitor [capacitance=100µF package="200 mil [THT, electrolytic]"]
  C2 = Electrolytic Capacitor [capacitance=100µF package="200 mil [THT, electrolytic]"]

nets:
  VCC: JP1.VCC, Bauteil1.VIN, hc-sr1.VCC, hc-sr2.VCC, NEOPIXEL1.+5V, NEOPIXEL2.+5V, C1.+, C2.+
  GND: JP1.GND, Bauteil1.GND, hc-sr1.GND, hc-sr2.GND, NEOPIXEL1.GND, NEOPIXEL2.GND, C1.-, C2.-
  N1: Bauteil1.D2, NEOPIXEL1.Din
  N2: Bauteil1.D3, hc-sr1.Trig
  N3: Bauteil1.D4, hc-sr1.Echo
  N4: Bauteil1.D6, NEOPIXEL2.Din
  N5: Bauteil1.D7, hc-sr2.Trig
  N6: Bauteil1.D8, hc-sr2.Echo

custom parts:
  Neopixel Strip -- Black (30/m): These NeoPixel strips have 30 digitally-addressable pixel LEDs per meter and are very affordable and are only 12.5 mm wide, 10 mm if you remove the strip from the casing.
